// Logisim project SAP-1.circ as structural Verilog
module SAP_1 (
  input  [3:0] in_1
);

  wire button_1_out, clock_1_out, controller_1_cp, controller_1_ea, controller_1_ep, controller_1_eu,
       controller_1_nce, controller_1_nei, controller_1_nla, controller_1_nlb, controller_1_nli,
       controller_1_nlm, controller_1_nlo, controller_1_out_18, controller_1_su, n8_bit_register_1_out_11,
       n8_bit_register_1_out_12, n8_bit_register_1_out_13, n8_bit_register_1_out_14, not_1_out, not_2_out,
       not_3_out, not_4_out, not_5_out, not_6_out, not_7_out, not_8_out, not_9_out, not_10_out, or_1_out;
  wire [3:0] controlled_buffer_2_out, MAR_q, multiplexer_1_out, n8_bit_register_1_out_18;
  wire [7:0] adder_1_out, controlled_buffer_1_out, controlled_buffer_4_out, controlled_buffer_5_out,
       controlled_buffer_6_out, program_counter_1__0, register_1_q, register_2_q, register_3_q,
       subtractor_1_out;

  not not_1 (not_1_out, or_1_out);
  not not_2 (not_2_out, not_6_out);
  not not_3 (not_3_out, controller_1_nce);
  Clock clock_1 (.out(clock_1_out));
  not not_4 (not_4_out, controller_1_nlm);
  assign controlled_buffer_1_out = not_5_out ? program_counter_1__0 : 8'bz;  // Controlled_Buffer controlled_buffer_1
  not not_5 (not_5_out, controller_1_nli);
  _8_bit_register u_8_bit_register_1 (
    .in_9(clock_1_out), .in_10(or_1_out), .in_1(controlled_buffer_1_out[7]),
    .in_2(controlled_buffer_1_out[6]), .in_3(controlled_buffer_1_out[5]), .in_4(controlled_buffer_1_out[4]),
    .in_5(controlled_buffer_1_out[3]), .in_6(controlled_buffer_1_out[2]), .in_7(controlled_buffer_1_out[1]),
    .in_8(controlled_buffer_1_out[0]), .out_11(n8_bit_register_1_out_11), .out_12(n8_bit_register_1_out_12),
    .out_13(n8_bit_register_1_out_13), .out_14(n8_bit_register_1_out_14),
    .out_15(n8_bit_register_1_out_18[3]), .out_16(n8_bit_register_1_out_18[2]),
    .out_17(n8_bit_register_1_out_18[1]), .out_18(n8_bit_register_1_out_18[0]));
  not not_6 (not_6_out, clock_1_out);
  Program_Counter program_counter_1 (
    .Cp(controller_1_cp), .nCLK(not_2_out), .nCLR(not_1_out), .Ep(controller_1_ep),
    ._0(program_counter_1__0[0]), ._1(program_counter_1__0[1]), ._2(program_counter_1__0[2]),
    ._3(program_counter_1__0[3]));
  assign controlled_buffer_2_out = not_4_out ? program_counter_1__0[3:0] : 4'bz;  // Controlled_Buffer controlled_buffer_2
  Controller controller_1 (
    .CLK(clock_1_out), .CLR(or_1_out), .Cp(controller_1_cp), .Ep(controller_1_ep), .nLm(controller_1_nlm),
    .nCE(controller_1_nce), .nLi(controller_1_nli), .nEi(controller_1_nei), .nLa(controller_1_nla),
    .Ea(controller_1_ea), .Su(controller_1_su), .Eu(controller_1_eu), .nLb(controller_1_nlb),
    .nLo(controller_1_nlo), .I7(n8_bit_register_1_out_11), .I6(n8_bit_register_1_out_12),
    .I5(n8_bit_register_1_out_13), .I4(n8_bit_register_1_out_14), .out_18(controller_1_out_18));
  not not_7 (not_7_out, controller_1_nei);
  Register #(.width(4)) MAR (.D(controlled_buffer_2_out), .Q(MAR_q), .clk(clock_1_out));  // open: en, clr
  RAM #(.addrWidth(4)) ram_1 (
    .addr(multiplexer_1_out), .data(program_counter_1__0), .sel(not_3_out), .clk(clock_1_out));  // open: ld, clr
  assign program_counter_1__0[3:0] = not_7_out ? n8_bit_register_1_out_18 : 4'bz;  // Controlled_Buffer controlled_buffer_3
  or or_1 (or_1_out, button_1_out, controller_1_out_18);
  Multiplexer #(.width(4)) multiplexer_1 (.in0(in_1), .in1(MAR_q), .out(multiplexer_1_out), .sel(1'b1));  // open: en
  Button button_1 (.out(button_1_out));
  assign controlled_buffer_4_out = not_8_out ? program_counter_1__0 : 8'bz;  // Controlled_Buffer controlled_buffer_4
  not not_8 (not_8_out, controller_1_nlo);
  Register register_1 (.D(controlled_buffer_5_out), .Q(register_1_q), .clk(clock_1_out));  // open: en, clr
  assign controlled_buffer_5_out = not_10_out ? program_counter_1__0 : 8'bz;  // Controlled_Buffer controlled_buffer_5
  Multiplexer #(.width(8)) multiplexer_2 (
    .in0(adder_1_out), .in1(subtractor_1_out), .out(program_counter_1__0), .sel(controller_1_su),
    .en(controller_1_eu));
  assign controlled_buffer_6_out = not_9_out ? program_counter_1__0 : 8'bz;  // Controlled_Buffer controlled_buffer_6
  not not_9 (not_9_out, controller_1_nlb);
  Register register_2 (.D(controlled_buffer_4_out), .Q(register_2_q), .clk(clock_1_out));  // open: en, clr
  Adder adder_1 (.a(register_1_q), .b(register_3_q), .out(adder_1_out));  // open: cin, cout
  Subtractor subtractor_1 (.a(register_1_q), .b(register_3_q), .out(subtractor_1_out));  // open: bin, bout
  Register register_3 (.D(controlled_buffer_6_out), .Q(register_3_q), .clk(clock_1_out));  // open: en, clr
  assign program_counter_1__0 = controller_1_ea ? register_1_q : 8'bz;  // Controlled_Buffer controlled_buffer_7
  Hex_Digit_Display hex_digit_display_1 (.value(register_2_q[7:4]));  // open: dp
  Hex_Digit_Display hex_digit_display_2 (.value(register_2_q[3:0]));  // open: dp
  not not_10 (not_10_out, controller_1_nla);
endmodule

module Program_Counter (
  input  Cp,
  input  nCLK,
  input  nCLR,
  input  Ep,
  output _0,
  output _1,
  output _2,
  output _3
);

  wire j_k_ff_1_q, j_k_ff_2_q, j_k_ff_3_q, j_k_ff_4_q, not_1_out, not_2_out;

  not not_1 (not_1_out, nCLK);
  not not_2 (not_2_out, nCLR);
  J_K_Flip_Flop #(.trigger("falling")) j_k_ff_1 (
    .J(Cp), .clk(not_1_out), .K(Cp), .Q(j_k_ff_1_q), .reset(not_2_out));  // open: Qn, preset, en
  assign _0 = Ep ? j_k_ff_1_q : 1'bz;  // Controlled_Buffer controlled_buffer_1
  J_K_Flip_Flop #(.trigger("falling")) j_k_ff_2 (
    .J(Cp), .clk(j_k_ff_1_q), .K(Cp), .Q(j_k_ff_2_q), .reset(not_2_out));  // open: Qn, preset, en
  assign _1 = Ep ? j_k_ff_2_q : 1'bz;  // Controlled_Buffer controlled_buffer_2
  J_K_Flip_Flop #(.trigger("falling")) j_k_ff_3 (
    .J(Cp), .clk(j_k_ff_2_q), .K(Cp), .Q(j_k_ff_3_q), .reset(not_2_out));  // open: Qn, preset, en
  assign _2 = Ep ? j_k_ff_3_q : 1'bz;  // Controlled_Buffer controlled_buffer_3
  J_K_Flip_Flop #(.trigger("falling")) j_k_ff_4 (
    .J(Cp), .clk(j_k_ff_3_q), .K(Cp), .Q(j_k_ff_4_q), .reset(not_2_out));  // open: Qn, preset, en
  assign _3 = Ep ? j_k_ff_4_q : 1'bz;  // Controlled_Buffer controlled_buffer_4
endmodule

module Ring_Counter (
  input  CLK,
  input  nCLR,
  output T6,
  output T5,
  output T4,
  output T3,
  output T2,
  output T1
);

  wire not_1_out, not_2_out;

  D_Flip_Flop d_ff_1 (.clk(not_2_out), .D(T5), .Q(T6), .reset(not_1_out));  // open: Qn, preset, en
  D_Flip_Flop d_ff_2 (.clk(not_2_out), .D(T4), .Q(T5), .reset(not_1_out));  // open: Qn, preset, en
  D_Flip_Flop d_ff_3 (.clk(not_2_out), .D(T3), .Q(T4), .reset(not_1_out));  // open: Qn, preset, en
  D_Flip_Flop d_ff_4 (.clk(not_2_out), .D(T2), .Q(T3), .reset(not_1_out));  // open: Qn, preset, en
  D_Flip_Flop d_ff_5 (.clk(not_2_out), .D(T1), .Q(T2), .reset(not_1_out));  // open: Qn, preset, en
  not not_1 (not_1_out, nCLR);
  D_Flip_Flop d_ff_6 (.clk(not_2_out), .D(T6), .Q(T1), .preset(not_1_out));  // open: Qn, en, reset
  not not_2 (not_2_out, CLK);
endmodule

module Controller (
  input  I7,
  input  I6,
  input  I5,
  input  I4,
  input  CLK,
  input  CLR,
  output Cp,
  output Ep,
  output nLm,
  output nCE,
  output nLi,
  output nEi,
  output nLa,
  output Ea,
  output Su,
  output Eu,
  output nLb,
  output out_18,
  output nLo
);

  wire not_1_out, ring_counter_1_t1, ring_counter_1_t2, ring_counter_1_t3, ring_counter_1_t4,
       ring_counter_1_t5, ring_counter_1_t6;

  and and_1 (out_18, I4, I5, I6, I7);
  Ring_Counter ring_counter_1 (
    .CLK(CLK), .nCLR(not_1_out), .T6(ring_counter_1_t6), .T5(ring_counter_1_t5), .T4(ring_counter_1_t4),
    .T3(ring_counter_1_t3), .T2(ring_counter_1_t2), .T1(ring_counter_1_t1));
  control_matrix_complete control_matrix_complete_1 (
    .I7(I7), .Cp(Cp), .I6(I6), .Ep(Ep), .I5(I5), .Lm0(nLm), .I4(I4), .T6(ring_counter_1_t6), .CE0(nCE),
    .T5(ring_counter_1_t5), .T4(ring_counter_1_t4), .Li0(nLi), .T3(ring_counter_1_t3), .Ei0(nEi),
    .T2(ring_counter_1_t2), .T1(ring_counter_1_t1), .La0(nLa), .Ea0(Ea), .Su(Su), .Eu(Eu), .Lb0(nLb),
    .Lo0(nLo));
  not not_1 (not_1_out, CLR);
endmodule

module control_matrix_complete (
  input  I7,
  input  I6,
  input  I5,
  input  I4,
  input  T6,
  input  T5,
  input  T4,
  input  T3,
  input  T2,
  input  T1,
  output Cp,
  output Ep,
  output Lm0,
  output CE0,
  output Li0,
  output Ei0,
  output La0,
  output Ea0,
  output Su,
  output Eu,
  output Lb0,
  output Lo0
);

  wire and_1_out, and_2_out, and_3_out, and_4_out, and_5_out, and_6_out, and_7_out, and_8_out, and_11_out,
       and_12_out, and_13_out, not_1_out, not_2_out, not_3_out, not_4_out, not_5_out, not_6_out, not_8_out,
       not_9_out, not_10_out, not_11_out, not_12_out, not_13_out, not_14_out, not_15_out, not_16_out,
       not_17_out, not_18_out, not_19_out, not_20_out, not_21_out, not_22_out, not_23_out, not_24_out;

  not not_1 (not_1_out, T4);
  not not_2 (not_2_out, T1);
  not not_3 (not_3_out, T1);
  not not_4 (not_4_out, T5);
  not not_5 (not_5_out, T3);
  not not_6 (not_6_out, T3);
  not not_7 (Li0, T3);
  not not_8 (not_8_out, T4);
  not not_9 (not_9_out, I5);
  not not_10 (not_10_out, I4);
  not not_11 (not_11_out, T5);
  not not_12 (not_12_out, T6);
  not not_13 (not_13_out, T5);
  not not_14 (not_14_out, T6);
  not not_15 (not_15_out, T6);
  not not_16 (not_16_out, I4);
  not not_17 (not_17_out, I6);
  not not_18 (not_18_out, I6);
  not not_19 (not_19_out, I6);
  not not_20 (not_20_out, I5);
  not not_21 (not_21_out, I4);
  not not_22 (not_22_out, I7);
  not not_23 (not_23_out, T4);
  and and_1 (and_1_out, not_1_out, not_2_out);
  and and_2 (and_2_out, I6, not_3_out);
  and and_3 (and_3_out, not_4_out, not_5_out);
  and and_4 (and_4_out, I6, not_6_out);
  or or_1 (Ei0, not_8_out, I7);
  and and_5 (and_5_out, not_9_out, not_10_out, not_11_out);
  and and_6 (and_6_out, not_12_out, not_13_out);
  and and_7 (and_7_out, I4, not_14_out);
  and and_8 (and_8_out, I5, not_15_out);
  and and_9 (Ea0, I6, not_16_out, T4);
  and and_10 (Su, not_17_out, I5, T6);
  and and_11 (and_11_out, not_18_out, I4, T6);
  and and_12 (and_12_out, not_19_out, I5, T6);
  and and_13 (and_13_out, not_20_out, not_21_out);
  not not_24 (not_24_out, T5);
  or or_2 (Lo0, not_22_out, not_23_out, I4);
  or or_3 (Lm0, and_1_out, and_2_out);
  or or_4 (CE0, and_3_out, and_4_out);
  or or_5 (La0, and_5_out, and_6_out, and_7_out, and_8_out, I7);
  or or_6 (Eu, and_11_out, and_12_out);
  or or_7 (Lb0, and_13_out, not_24_out, I7);

  assign Cp = T2;
  assign Ep = T1;
endmodule

module _8_bit_register (
  input  in_1,
  input  in_2,
  input  in_3,
  input  in_4,
  input  in_5,
  input  in_6,
  input  in_7,
  input  in_8,
  input  in_9,
  input  in_10,
  output out_11,
  output out_12,
  output out_13,
  output out_14,
  output out_15,
  output out_16,
  output out_17,
  output out_18
);

  D_Flip_Flop d_ff_1 (.clk(in_9), .D(in_1), .Q(out_11), .reset(in_10));  // open: Qn, preset, en
  D_Flip_Flop d_ff_2 (.clk(in_9), .D(in_2), .Q(out_12), .reset(in_10));  // open: Qn, preset, en
  D_Flip_Flop d_ff_3 (.clk(in_9), .D(in_3), .Q(out_13), .reset(in_10));  // open: Qn, preset, en
  D_Flip_Flop d_ff_4 (.clk(in_9), .D(in_4), .Q(out_14), .reset(in_10));  // open: Qn, preset, en
  D_Flip_Flop d_ff_5 (.clk(in_9), .D(in_5), .Q(out_15), .reset(in_10));  // open: Qn, preset, en
  D_Flip_Flop d_ff_6 (.clk(in_9), .D(in_6), .Q(out_16), .reset(in_10));  // open: Qn, preset, en
  D_Flip_Flop d_ff_7 (.clk(in_9), .D(in_7), .Q(out_17), .reset(in_10));  // open: Qn, preset, en
  D_Flip_Flop d_ff_8 (.clk(in_9), .D(in_8), .Q(out_18), .reset(in_10));  // open: Qn, preset, en
endmodule
